// Logisim project EX01.circ as structural Verilog: 1 circuit, main circuit main
module main (
  input  a,
  input  b,
  input  a_2,
  input  b_2,
  output na___b__prime,
  output na___b__prime_2
);

  wire nor_1_out, nor_2_out, nor_4_out, nor_5_out;

  nor nor_1 (nor_1_out, a, a);
  nor nor_2 (nor_2_out, b_2, b_2);
  nor nor_3 (na___b__prime, nor_1_out, b);
  nor nor_4 (nor_4_out, a_2, a_2);
  nor nor_5 (nor_5_out, nor_2_out, nor_2_out);
  nor nor_6 (na___b__prime_2, nor_4_out, nor_5_out);

  // Notes on the sheet:
  //   (a & ~b)
  //   SIMPLIFICADO
  //   ~a
  //   OU
  //   ~b
  //   (~a + b)' = (a & ~b)
  //   ~a
  //   b
endmodule
