// Logisim project EX02.circ as structural Verilog: 1 circuit, main circuit main
module main (
  input  a,
  input  b,
  input  a_2,
  input  b_2,
  output a___nb__prime,
  output a___nb__prime_2
);

  wire nand_1_out, nand_2_out, nand_4_out, nand_5_out;

  nand nand_1 (nand_1_out, b, b);
  nand nand_2 (nand_2_out, a_2, a_2);
  nand nand_3 (a___nb__prime, a, nand_1_out);
  nand nand_4 (nand_4_out, nand_2_out, nand_2_out);
  nand nand_5 (nand_5_out, b_2, b_2);
  nand nand_6 (a___nb__prime_2, nand_4_out, nand_5_out);

  // Notes on the sheet:
  //   (~a | b)
  //   SIMPLIFICADO
  //   ~b
  //   OU
  //   ~a
  //   (a . ~b)' = (~a | b)
  //   a
  //   ~b
endmodule
