// Logisim project EX03.circ as structural Verilog: 1 circuit, main circuit main
module main (
  input  a,
  input  b,
  output a___nb__prime
);

  wire nor_1_out;

  nor nor_1 (nor_1_out, b, b);
  nor nor_2 (a___nb__prime, a, nor_1_out);

  // Notes on the sheet:
  //   ~(a | ~b)
  //   SIMPLIFICADO
  //   ~b
  //   (a + ~b)' = ~(a | ~b) = (~a & b)
endmodule
