// Logisim project EX04.circ as structural Verilog: 1 circuit, main circuit main
module main (
  input  a,
  input  b,
  output a___nb__prime
);

  wire nand_1_out;

  nand nand_1 (nand_1_out, b, b);
  nand nand_2 (a___nb__prime, a, nand_1_out);

  // Notes on the sheet:
  //   ~(a & ~b)
  //   SIMPLIFICADO
  //   ~b
  //   (a . ~b)' = ~(a & ~b) = (~a | b)
endmodule
