// Logisim project EX05.circ as structural Verilog: 1 circuit, main circuit main
module main (
  input  a,
  input  b,
  output out_3,
  output a___b
);

  wire nor_1_out, nor_2_out, nor_3_out, nor_4_out;

  nor nor_1 (nor_1_out, a, a);
  nor nor_2 (nor_2_out, b, b);
  nor nor_3 (nor_3_out, a, b);
  nor nor_4 (nor_4_out, nor_1_out, nor_2_out);
  nor nor_5 (out_3, nor_4_out, nor_3_out);
  xor xor_1 (a___b, b, a);

  // Notes on the sheet:
  //   a
  //   b
  //   (a ^ b)
  //   ~a
  //   ~b
  //   (a + b)'
  //   ~(a + b) = (~a . ~b)
  //   EQUIVALENTE AND
  //   (~a + ~b)'
  //    ~(~a + ~b) = (a . b)
  //   XOR
  //   (a ^ b)
  //   (a . b) + (~a . ~b)
  //   (a . ~b) + (~a . b)
  //   Equivalente à: (a ^ b)
endmodule
