// Logisim project EX06.circ as structural Verilog: 1 circuit, main circuit main
module main (
  input  a,
  input  b,
  output out_3,
  output n_a___b
);

  wire nand_1_out, nand_2_out, nand_3_out, nand_4_out;

  nand nand_1 (nand_1_out, a, a);
  nand nand_2 (nand_2_out, b, b);
  nand nand_3 (nand_3_out, a, b);
  nand nand_4 (nand_4_out, nand_1_out, nand_2_out);
  nand nand_5 (out_3, nand_4_out, nand_3_out);
  xnor xnor_1 (n_a___b, b, a);

  // Notes on the sheet:
  //   a
  //   b
  //   ~(a ^ b)
  //   ~a
  //   ~b
  //   (a . b)'
  //   ~(a . b) = (~a + ~b)
  //   (~a . ~b)'
  //   EQUIVALENTE OR
  //    ~(~a . ~b) = (a + b)
  //   XNOR
  //   ~(a ^ b)
  //   (a + b) + (~a + ~b)
  //   (a + ~b) + (~a + b)
  //   Equivalente à: ~(a ^ b)
endmodule
