// Logisim project EX07.circ as structural Verilog: 1 circuit, main circuit main
module main (
  input  a,
  input  b,
  output n_a___b,
  output out_4,
  output out_5
);

  wire _1_out, _2_out, _3_out, _4_out, _5_out;

  nor _1 (_1_out, a, a);
  nor _2 (_2_out, b, b);
  nor _4 (_4_out, a, b);
  xnor xnor_1 (out_4, a, b);
  xor xor_1 (out_5, a, b);
  nor _3 (_3_out, _1_out, _2_out);
  nor _5 (_5_out, _3_out, _4_out);
  nor nor_1 (n_a___b, _5_out, _5_out);

  // Notes on the sheet:
  //   a
  //   b
  //   XNOR
  //   (a ^ b) = ~(~a ^ ~b)
  //   OU SEJA, EQUIVALENTE XOR
  //   CONTRÁRIO DO XOR
  //   XOR
  //   ~(~a ^ ~b)
  //   1, 2, 3, 4 e 5: EQUIVALENTE XOR
  //   1, 2 e 3: EQUIVALENTE AND
  //   ~a
  //   ~b
  //   (a + b)'
  //   Negar a entrada pra depois negar a saída é igual à não negar nada!
  //   (~a + ~b)
  //   (a ^ b)
endmodule
