// Logisim project EX08.circ as structural Verilog: 1 circuit, main circuit main
module main (
  input  a,
  input  b,
  output na___nb__prime
);

  wire nand_1_out, nand_2_out;

  nand nand_1 (nand_1_out, a, a);
  nand nand_2 (nand_2_out, b, b);
  nand nand_3 (na___nb__prime, nand_1_out, nand_2_out);

  // Notes on the sheet:
  //   (~a | ~b)
  //   ~a
  //   ~b
  //   ~(~a . ~b)) = (a + b)
  //   OU SEJA, EQUIVALENTE OR
endmodule
