// Logisim project Exercicios.circ as structural Verilog
module Ex1 (
  input  x,
  input  y,
  input  z,
  output out_4,
  output out_5,
  output out_6,
  output out_7,
  output out_8
);

  wire and_1_out, and_2_out, and_3_out, and_4_out, and_5_out, and_6_out, and_7_out, and_8_out, and_9_out,
       and_10_out, and_11_out, not_1_out, not_2_out, not_3_out, not_4_out, not_5_out, not_6_out, not_7_out,
       not_8_out, not_9_out, not_10_out, not_11_out, not_12_out;

  not not_1 (not_1_out, y);
  not not_2 (not_2_out, z);
  not not_3 (not_3_out, y);
  not not_4 (not_4_out, z);
  not not_5 (not_5_out, x);
  not not_6 (not_6_out, z);
  not not_7 (not_7_out, x);
  not not_8 (not_8_out, y);
  not not_9 (not_9_out, x);
  not not_10 (not_10_out, z);
  not not_11 (not_11_out, y);
  not not_12 (not_12_out, z);
  and and_1 (and_1_out, x, z);
  and and_2 (and_2_out, not_1_out, z);
  and and_3 (and_3_out, x, not_2_out);
  and and_4 (and_4_out, not_3_out, not_4_out);
  and and_5 (and_5_out, not_5_out, z);
  and and_6 (and_6_out, y, not_6_out);
  and and_7 (and_7_out, not_7_out, y);
  and and_8 (and_8_out, not_8_out, z);
  and and_9 (and_9_out, not_9_out, not_10_out);
  and and_10 (and_10_out, not_11_out, not_12_out);
  and and_11 (and_11_out, x, y, z);
  or or_1 (out_4, and_1_out, and_2_out);
  or or_2 (out_5, and_3_out, and_4_out);
  or or_3 (out_6, and_5_out, and_6_out);
  or or_4 (out_7, and_7_out, and_8_out);
  or or_5 (out_8, and_9_out, and_10_out, and_11_out);

  // Notes on the sheet:
  //   a)
  //   b)
  //   c)
  //   d)
  //   e)
  //   Exercício 1
endmodule

module Ex2 (
  input  X,
  input  Y,
  input  Z,
  output out_4,
  output out_5,
  output out_6,
  output out_7,
  output out_8
);

  wire not_1_out, not_2_out, not_3_out, not_4_out, not_5_out, not_6_out, not_7_out, not_8_out, not_9_out,
       not_10_out, not_11_out, not_12_out, or_1_out, or_2_out, or_3_out, or_4_out, or_5_out, or_6_out,
       or_7_out, or_8_out, or_9_out, or_10_out, or_11_out, or_12_out;

  not not_1 (not_1_out, Z);
  not not_2 (not_2_out, X);
  not not_3 (not_3_out, Z);
  not not_4 (not_4_out, X);
  not not_5 (not_5_out, Z);
  not not_6 (not_6_out, Y);
  not not_7 (not_7_out, Z);
  not not_8 (not_8_out, X);
  not not_9 (not_9_out, Y);
  not not_10 (not_10_out, X);
  not not_11 (not_11_out, Y);
  not not_12 (not_12_out, Z);
  or or_1 (or_1_out, Y, not_1_out);
  or or_2 (or_2_out, not_2_out, not_3_out);
  or or_3 (or_3_out, not_4_out, Z);
  or or_4 (or_4_out, Y, Z);
  or or_5 (or_5_out, X, not_5_out);
  or or_6 (or_6_out, not_6_out, Z);
  or or_7 (or_7_out, X, Y);
  or or_8 (or_8_out, Y, not_7_out);
  or or_9 (or_9_out, not_8_out, not_9_out, Z);
  or or_10 (or_10_out, X, Z);
  or or_11 (or_11_out, Y, Z);
  or or_12 (or_12_out, not_10_out, not_11_out, not_12_out);
  and and_1 (out_4, or_1_out, or_2_out);
  and and_2 (out_5, or_3_out, or_4_out);
  and and_3 (out_6, or_5_out, or_6_out);
  and and_4 (out_7, or_7_out, or_8_out, or_9_out);
  and and_5 (out_8, or_10_out, or_11_out, or_12_out);

  // Notes on the sheet:
  //   a)
  //   b)
  //   c)
  //   d)
  //   e)
  //   Exercício 2
endmodule

module Ex3 (
  input  x,
  input  y,
  input  w,
  input  z,
  output out_5,
  output out_6,
  output out_7,
  output out_8,
  output out_9
);

  wire and_1_out, and_2_out, and_3_out, and_4_out, and_5_out, and_6_out, and_7_out, and_8_out, and_9_out,
       and_10_out, and_11_out, and_12_out, and_13_out, and_14_out, and_15_out, and_16_out, and_17_out,
       and_18_out, and_19_out, and_20_out, and_21_out, and_22_out, not_1_out, not_2_out, not_3_out,
       not_4_out, not_5_out, not_6_out, not_7_out, not_8_out, not_9_out, not_10_out, not_11_out, not_12_out,
       not_13_out, not_14_out, not_15_out, not_16_out, not_17_out, not_18_out, not_19_out, not_20_out,
       not_21_out, not_22_out, not_23_out, not_24_out, not_25_out, not_26_out, not_27_out, not_28_out,
       not_29_out, not_30_out, not_31_out, not_32_out, not_33_out, not_34_out, not_35_out, not_36_out;

  not not_1 (not_1_out, x);
  not not_2 (not_2_out, z);
  not not_3 (not_3_out, z);
  not not_4 (not_4_out, w);
  not not_5 (not_5_out, z);
  not not_6 (not_6_out, x);
  not not_7 (not_7_out, y);
  not not_8 (not_8_out, w);
  not not_9 (not_9_out, x);
  not not_10 (not_10_out, y);
  not not_11 (not_11_out, w);
  not not_12 (not_12_out, z);
  not not_13 (not_13_out, x);
  not not_14 (not_14_out, y);
  not not_15 (not_15_out, z);
  not not_16 (not_16_out, x);
  not not_17 (not_17_out, y);
  not not_18 (not_18_out, w);
  not not_19 (not_19_out, x);
  not not_20 (not_20_out, y);
  not not_21 (not_21_out, w);
  not not_22 (not_22_out, y);
  not not_23 (not_23_out, w);
  not not_24 (not_24_out, y);
  and and_1 (and_1_out, not_1_out, w, not_2_out);
  and and_2 (and_2_out, y, w, not_3_out);
  and and_3 (and_3_out, x, not_4_out, not_5_out);
  and and_4 (and_4_out, not_6_out, not_7_out, not_8_out, z);
  and and_5 (and_5_out, not_9_out, not_10_out, not_11_out);
  and and_6 (and_6_out, y, w, z);
  and and_7 (and_7_out, x, w, z);
  and and_8 (and_8_out, x, w, not_12_out);
  and and_9 (and_9_out, not_13_out, not_14_out, w, not_15_out);
  and and_10 (and_10_out, not_16_out, not_17_out, not_18_out);
  and and_11 (and_11_out, not_19_out, not_20_out, z);
  and and_12 (and_12_out, y, not_21_out, z);
  and and_13 (and_13_out, x, not_22_out, not_23_out);
  and and_14 (and_14_out, x, not_24_out, z);
  or or_1 (out_5, and_1_out, and_2_out, and_3_out, and_4_out);
  or or_2 (out_7, and_5_out, and_6_out, and_7_out, and_8_out, and_9_out);
  or or_3 (out_9, and_10_out, and_11_out, and_12_out, and_13_out, and_14_out);
  not not_25 (not_25_out, x);
  not not_26 (not_26_out, y);
  not not_27 (not_27_out, w);
  not not_28 (not_28_out, x);
  not not_29 (not_29_out, w);
  not not_30 (not_30_out, z);
  not not_31 (not_31_out, x);
  not not_32 (not_32_out, w);
  not not_33 (not_33_out, w);
  not not_34 (not_34_out, x);
  not not_35 (not_35_out, z);
  not not_36 (not_36_out, z);
  and and_15 (and_15_out, not_25_out, not_26_out, not_27_out);
  and and_16 (and_16_out, not_28_out, w, z);
  and and_17 (and_17_out, y, w, z);
  and and_18 (and_18_out, x, not_29_out, not_30_out);
  and and_19 (and_19_out, not_31_out, y, not_32_out);
  and and_20 (and_20_out, y, not_33_out, z);
  and and_21 (and_21_out, not_34_out, w, not_35_out);
  and and_22 (and_22_out, x, w, not_36_out);
  or or_4 (out_6, and_15_out, and_16_out, and_17_out, and_18_out);
  or or_5 (out_8, and_19_out, and_20_out, and_21_out, and_22_out);

  // Notes on the sheet:
  //   Exercício 3
  //   a)
  //   c)
  //   e)
  //   b)
  //   y
  //   x
  //   d)
  //   y
  //   x
  //   z
  //   w
  //   z
  //   w
endmodule

module Ex4 (
  input  X,
  input  Y,
  input  W,
  input  Z,
  output out_5,
  output out_6,
  output out_7,
  output out_8,
  output out_9
);

  wire not_1_out, not_2_out, not_3_out, not_4_out, not_5_out, not_6_out, not_7_out, not_8_out, not_9_out,
       not_10_out, not_11_out, not_12_out, not_13_out, not_14_out, not_15_out, not_16_out, not_17_out,
       not_18_out, not_19_out, not_20_out, not_21_out, not_22_out, not_23_out, not_24_out, not_25_out,
       not_26_out, not_27_out, not_28_out, not_29_out, not_30_out, not_31_out, or_1_out, or_2_out, or_3_out,
       or_4_out, or_5_out, or_6_out, or_7_out, or_8_out, or_9_out, or_10_out, or_11_out, or_12_out,
       or_13_out, or_14_out, or_15_out, or_16_out, or_17_out;

  not not_1 (not_1_out, Y);
  not not_2 (not_2_out, Z);
  not not_3 (not_3_out, Y);
  not not_4 (not_4_out, Z);
  not not_5 (not_5_out, W);
  not not_6 (not_6_out, Y);
  not not_7 (not_7_out, X);
  not not_8 (not_8_out, Y);
  not not_9 (not_9_out, W);
  not not_10 (not_10_out, Z);
  not not_11 (not_11_out, W);
  not not_12 (not_12_out, Y);
  not not_13 (not_13_out, W);
  not not_14 (not_14_out, W);
  not not_15 (not_15_out, Z);
  not not_16 (not_16_out, Y);
  not not_17 (not_17_out, W);
  not not_18 (not_18_out, X);
  not not_19 (not_19_out, Y);
  not not_20 (not_20_out, Z);
  or or_1 (or_1_out, X, not_1_out, not_2_out);
  or or_2 (or_2_out, not_3_out, W, not_4_out);
  or or_3 (or_3_out, X, Y, not_5_out, Z);
  or or_4 (or_4_out, not_6_out, W, Z);
  or or_5 (or_5_out, not_7_out, Y, Z);
  or or_6 (or_6_out, X, not_8_out, not_9_out, not_10_out);
  or or_7 (or_7_out, X, Y, not_11_out);
  or or_8 (or_8_out, X, not_12_out, not_13_out);
  or or_9 (or_9_out, Y, not_14_out, not_15_out);
  or or_10 (or_10_out, not_16_out, not_17_out, Z);
  or or_11 (or_11_out, not_18_out, not_19_out, W, not_20_out);
  and and_1 (out_5, or_1_out, or_2_out, or_3_out);
  and and_2 (out_7, or_4_out, or_5_out, or_6_out);
  and and_3 (out_9, or_7_out, or_8_out, or_9_out, or_10_out, or_11_out);
  not not_21 (not_21_out, Y);
  not not_22 (not_22_out, W);
  not not_23 (not_23_out, X);
  not not_24 (not_24_out, Z);
  not not_25 (not_25_out, Y);
  not not_26 (not_26_out, Z);
  not not_27 (not_27_out, Y);
  not not_28 (not_28_out, Z);
  not not_29 (not_29_out, Y);
  not not_30 (not_30_out, W);
  not not_31 (not_31_out, Z);
  or or_12 (or_12_out, not_21_out, not_22_out, Z);
  or or_13 (or_13_out, not_23_out, Y, not_24_out);
  or or_14 (or_14_out, X, not_25_out, W, Z);
  or or_15 (or_15_out, X, W, not_26_out);
  or or_16 (or_16_out, not_27_out, W, not_28_out);
  or or_17 (or_17_out, not_29_out, not_30_out, not_31_out);
  and and_4 (out_6, or_12_out, or_13_out, or_14_out);
  and and_5 (out_8, or_15_out, or_16_out, or_17_out);

  // Notes on the sheet:
  //   Exercício 4
  //   a)
  //   c)
  //   e)
  //   b)
  //   d)
  //   y
  //   z
  //   w
  //   x
  //   w
  //   y
  //   z
  //   x
endmodule

module Ex5 (
  input  x,
  input  y,
  input  z,
  output s,
  output s1
);

  wire and_1_out, and_2_out, and_3_out, not_1_out, not_2_out, not_3_out, not_4_out, not_5_out, not_6_out,
       not_7_out, not_8_out, or_1_out, or_2_out, or_3_out;

  not not_1 (not_1_out, y);
  not not_2 (not_2_out, x);
  and and_1 (and_1_out, z, y);
  not not_3 (not_3_out, x);
  not not_4 (not_4_out, z);
  not not_5 (not_5_out, y);
  or or_1 (or_1_out, not_1_out, not_2_out);
  and and_2 (and_2_out, y, x);
  or or_2 (or_2_out, and_1_out, not_3_out);
  or or_3 (or_3_out, not_4_out, not_5_out);
  not not_6 (not_6_out, or_1_out);
  not not_7 (not_7_out, and_2_out);
  not not_8 (not_8_out, or_2_out);
  and and_3 (and_3_out, not_6_out, not_7_out);
  and and_4 (s1, or_3_out, x);
  or or_4 (s, and_3_out, not_8_out);

  // Notes on the sheet:
  //   Exercício 5
  //   EQUIVALENTE
  //   f (x,y,z) = m (4,5,6) = (x.z')+(x.y')
endmodule

module Ex6 (
  input  X,
  input  Y,
  input  W,
  input  Z,
  output S,
  output S1
);

  wire and_1_out, and_2_out, and_3_out, not_1_out, not_2_out, not_3_out, not_4_out, not_5_out, not_6_out,
       not_7_out, not_8_out, not_9_out, not_10_out, or_1_out, or_2_out, or_3_out;

  not not_1 (not_1_out, Y);
  not not_2 (not_2_out, X);
  not not_3 (not_3_out, W);
  and and_1 (and_1_out, Z, W, Y);
  not not_4 (not_4_out, X);
  not not_5 (not_5_out, Z);
  not not_6 (not_6_out, W);
  not not_7 (not_7_out, Y);
  or or_1 (or_1_out, not_1_out, W, not_2_out);
  and and_2 (and_2_out, Y, not_3_out, X);
  or or_2 (or_2_out, and_1_out, not_4_out);
  or or_3 (or_3_out, not_5_out, not_6_out, not_7_out);
  not not_8 (not_8_out, or_1_out);
  not not_9 (not_9_out, and_2_out);
  not not_10 (not_10_out, or_2_out);
  and and_3 (and_3_out, not_8_out, not_9_out);
  and and_4 (S1, or_3_out, X);
  or or_4 (S, and_3_out, not_10_out);

  // Notes on the sheet:
  //   Exercício 6
  //   EQUIVALENTE
  //   F (X,Y,W,Z) = M (0,1,2,3,4,5,6,7,15) = X.(Y'+W'+Z')
endmodule
