// Logisim project Exercicios.circ as structural Verilog: 8 circuits, main circuit main
module main (
  input  x,
  input  y,
  input  Carry_in,
  output out_4,
  output out_5,
  output BIT_0,
  output BIT_1
);

  wire and_2_out, and_3_out, xor_2_out;

  xor xor_1 (out_4, x, y);
  and and_1 (out_5, y, x);
  xor xor_2 (xor_2_out, x, y);
  and and_2 (and_2_out, x, y);
  // Probe on and_2_out
  xor xor_3 (BIT_0, Carry_in, xor_2_out);
  and and_3 (and_3_out, Carry_in, xor_2_out);
  // Probe on and_3_out
  or or_1 (BIT_1, and_3_out, and_2_out);

  // Notes on the sheet:
  //   x
  //   y
  //   x
  //   y
  //   Carry_out
endmodule

module _701 (
  input  select,
  input  x,
  input  y,
  output s,
  output s_2
);

  wire and1_2_out, and1_out, and2_out, and3_out, nand1_2_out, nand1_out, nand2_2_out, nand2_out, nand3_2_out,
       nand3_out, not1_2_out, not1_out;

  and and1 (and1_out, x, y);
  nand nand1 (nand1_out, x, y);
  and and1_2 (and1_2_out, x, y);
  nand nand1_2 (nand1_2_out, x, y);
  nand not1 (not1_out, select, select);
  nand not1_2 (not1_2_out, select, select);
  and and2 (and2_out, not1_out, and1_out);
  and and3 (and3_out, select, nand1_out);
  nand nand2 (nand2_out, not1_2_out, and1_2_out);
  nand nand3 (nand3_out, select, nand1_2_out);
  nand nand2_2 (nand2_2_out, and2_out, and2_out);
  nand nand3_2 (nand3_2_out, and3_out, and3_out);
  nand nand4 (s_2, nand2_out, nand3_out);
  nand nand4_2 (s, nand2_2_out, nand3_2_out);

  // Notes on the sheet:
  //   x
  //   y
  //   x
  //   y
  //   x
  //   y
  //   x
  //   y
  //   s_and
  //   s_nand
  //   s_and
  //   s_nand
  //   not_select
  //   Versão SIMPLIFICADA
  //   not_select
  //   select = 0 (AND)
  //   select = 1 (NAND)
  //   s1
  //   s2
  //   s1
  //   s2
  //   s3
  //   s4
endmodule

module _702 (
  input  select,
  input  x,
  input  y,
  output s,
  output s_2
);

  wire nor1_2_out, nor1_out, nor2_2_out, nor2_out, nor3_2_out, nor3_out, nor4_out, nor5_out, not1_2_out,
       not1_out, or1_out;

  nor nor1 (nor1_out, x, y);
  nor nor4 (nor4_out, x, y);
  or or1 (or1_out, x, y);
  nor nor1_2 (nor1_2_out, x, y);
  nor nor2 (nor2_out, select, nor1_out);
  nor not1 (not1_out, select, select);
  nor nor5 (nor5_out, nor4_out, nor4_out);
  nor not1_2 (not1_2_out, select, select);
  nor nor3 (nor3_out, not1_out, nor5_out);
  or or1_2 (s, nor2_out, nor3_out);
  nor nor2_2 (nor2_2_out, not1_2_out, or1_out);
  nor nor3_2 (nor3_2_out, select, nor1_2_out);
  or or2 (s_2, nor2_2_out, nor3_2_out);

  // Notes on the sheet:
  //   x
  //   y
  //   x
  //   y
  //   x
  //   y
  //   x
  //   y
  //   s_or
  //   s_nor
  //   s_or
  //   s_nor
  //   s2
  //   Versão SIMPLIFICADA
  //   select = 0 (OR)
  //   select = 1 (NOR)
  //   s1
  //   not_select
  //   s3
  //   not_select
  //   s1
  //   s2
endmodule

module _703 (
  input  k1,
  input  k0,
  input  x,
  input  y,
  output s
);

  wire and1_out, and2_out, and3_out, nand1_out, nand2_out, nand3_out, nand4_out, nor1_out, nor2_out,
       nor3_out, not1_out, not2_out, or1_out, or2_out;

  and and1 (and1_out, x, y);
  nand nand1 (nand1_out, x, y);
  or or1 (or1_out, x, y);
  nor nor1 (nor1_out, x, y);
  nand not1 (not1_out, k1, k1);
  nand nand2 (nand2_out, not1_out, and1_out);
  nand nand3 (nand3_out, k1, nand1_out);
  nor nor2 (nor2_out, not1_out, or1_out);
  nor nor3 (nor3_out, k1, nor1_out);
  or or2 (or2_out, nor2_out, nor3_out);
  nand nand4 (nand4_out, nand2_out, nand3_out);
  and and2 (and2_out, k0, nand4_out);
  nand not2 (not2_out, k0, k0);
  and and3 (and3_out, not2_out, or2_out);
  or or3 (s, and2_out, and3_out);

  // Notes on the sheet:
  //   x
  //   y
  //   x
  //   y
  //   x
  //   y
  //   x
  //   y
  //   s_and
  //   s_nand
  //   s_or
  //   s_nor
  //   k1 = 0 && k0 = 0 (OR)
  //   k1 = 0 && k0 = 1 (AND)
  //   k1 = 1 && k0 = 0 (NOR)
  //   k1
  //   k1 = 1 && k0 = 1 (NAND)
  //   not_k1
  //   s1
  //   k1
  //   s2
  //   not_k1
  //   s3
  //   s4
  //   k0
  //   s5
  //   s6
  //   not_k0
  //   A ordem está assim para dH de 1, para que sejam necessárias menas trocas por operação no verilog, sempre muda 1 bit apenas em vez de mudar 2 bits do 1(01) pro 2(10)
  //   s7
  //   s8
endmodule

module _704 (
  input  x,
  input  y,
  input  [1:0] select,
  output s
);

  wire nor1_out, or1_out, xnor1_out, xor1_out;

  xnor xnor1 (xnor1_out, x, y);
  xor xor1 (xor1_out, x, y);
  or or1 (or1_out, x, y);
  nor nor1 (nor1_out, x, y);
  Multiplexer #(.select(2), .enable("false")) multiplexer_1 (
    .in0(xnor1_out), .in1(xor1_out), .in2(or1_out), .in3(nor1_out), .out(s), .sel(select));

  // Notes on the sheet:
  //   x
  //   y
  //   x
  //   y
  //   x
  //   y
  //   x
  //   y
  //   s_xnor
  //   s_xor
  //   s_or
  //   s_nor
  //   11-NOR; 10-OR; 01-XOR; 00-XNOR
  //   01
  //   10
  //   00
  //   11
endmodule

module _705 (
  input  x,
  input  y,
  input  [2:0] select,
  output s
);

  wire and_1_out, nand_1_out, nor1_out, not_1_out, not_2_out, or1_out, xnor1_out, xor1_out;

  not not_1 (not_1_out, x);
  not not_2 (not_2_out, y);
  xnor xnor1 (xnor1_out, x, y);
  xor xor1 (xor1_out, x, y);
  or or1 (or1_out, x, y);
  nor nor1 (nor1_out, x, y);
  and and_1 (and_1_out, x, y);
  nand nand_1 (nand_1_out, x, y);
  Multiplexer #(.select(3), .enable("false")) multiplexer_1 (
    .in0(not_1_out), .in1(not_2_out), .in2(xnor1_out), .in3(xor1_out), .in4(or1_out), .in5(nor1_out),
    .in6(and_1_out), .in7(nand_1_out), .out(s), .sel(select));

  // Notes on the sheet:
  //   x
  //   y
  //   x
  //   y
  //   x
  //   y
  //   x
  //   y
  //   x
  //   y
  //   x
  //   y
  //   x
  //   y
  //   not_x
  //   not_y
  //   s_xnor
  //   s_xor
  //   s_or
  //   s_nor
  //   s_and
  //   s_nand
  //   011
  //   100
  //   000-NOT(x); 001-NOT(y); 010-XNOR; 011-XOR; 100-OR; 101-NOR; 110-AND; 111-NAND
  //   000
  //   001
  //   010
  //   101
  //   110
  //   111
endmodule

module _706 (
  input  [3:0] x,
  input  [3:0] y,
  input  select,
  output [3:0] s
);

  wire [3:0] xnor1_out, xor1_out;

  assign xnor1_out = ~(x ^ y);  // XNOR_Gate xnor1, 4 bits wide
  assign xor1_out = x ^ y;  // XOR_Gate xor1, 4 bits wide
  Multiplexer #(.width(4), .enable("false")) multiplexer_1 (.in0(xnor1_out), .in1(xor1_out), .out(s), .sel(select));

  // Notes on the sheet:
  //   x
  //   y
  //   x
  //   y
  //   1-IGUAL; 0-DIFERENTE
  //   s_xnor
  //   s_xor
  //   00
  //   01
endmodule

module _707 (
  input  [3:0] x,
  input  [3:0] y,
  input  Carry_in,
  output [3:0] out_4,
  output [3:0] out_5,
  output [3:0] BIT_0,
  output [3:0] BIT_1
);

  wire [3:0] and_2_out, and_3_out, xor_2_out;
  wire [3:1] undriven;

  assign out_4 = x ^ y;  // XOR_Gate xor_1, 4 bits wide
  assign out_5 = y & x;  // AND_Gate and_1, 4 bits wide
  assign xor_2_out = x ^ y;  // XOR_Gate xor_2, 4 bits wide
  assign and_2_out = x & y;  // AND_Gate and_2, 4 bits wide
  // Probe on and_2_out
  assign BIT_0 = {undriven, Carry_in} ^ xor_2_out;  // XOR_Gate xor_3, 4 bits wide
  assign and_3_out = {undriven, Carry_in} & xor_2_out;  // AND_Gate and_3, 4 bits wide
  // Probe on and_3_out
  assign BIT_1 = and_3_out | and_2_out;  // OR_Gate or_1, 4 bits wide

  // Notes on the sheet:
  //   x
  //   y
  //   x
  //   y
  //   Carry_out
endmodule
